# Fritzing sketch weatherdisplay (saved by Fritzing 0.9.3b)
breadboards: 1

parts:
  U2 = LCD-16X2 [package=lcd-16x2]
  Part1 = Arduino Uno (Rev3) - ICSP
  U3 = POT [package=pot_mammoth]
  DHT2 = DHT11 Humitidy and Temperature Sensor
  Part2 = Barometric Pressure Sensor - BMP085 Breakout

nets:
  GND: U2.VSS, U2.R_W, U2.K, Part1.GND, U3.S, DHT2.GND, Part2.GND
  VDD: U2.VDD, U2.A, Part1.5V, U3.E
  N1: U2.VO, U3.A
  N2: U2.RS, Part1.D11_PWM/MOSI
  N3: U2.E, Part1.D10_PWM/SS
  N4: U2.DB2, U2.DB3, U2.DB4, Part1.D5_PWM
  N5: U2.DB5, Part1.D4
  N6: U2.DB6, Part1.D3_PWM
  N7: U2.DB7, Part1.D2
  N8: Part1.A4/SDA, Part2.SDA
  N9: Part1.A5/SCL, Part2.SCL
  N10: Part1.D6_PWM, DHT2.DATA
  3V3: Part1.3V3, DHT2.VDD, Part2.VCC

custom parts:
  DHT11 Humitidy and Temperature Sensor: DHT11 Humidity and Temperature Sensor
